// Logisim project Tyler Quayle - Question 3.circ as structural Verilog: 1 circuit, main circuit main
module main (
  input  X,
  input  Y,
  input  Z,
  output A,
  output B,
  output C
);

  wire not_1_out, not_2_out, not_3_out, nX_nY_out, nXZ_out, nY_nZ_out, X_nZ_out, XYZ_out, XZ_out;

  not not_1 (not_1_out, X);
  not not_2 (not_2_out, Y);
  not not_3 (not_3_out, Z);
  and XZ (XZ_out, X, Z);
  and nX_nY (nX_nY_out, not_1_out, not_2_out);
  and XYZ (XYZ_out, Y, X, Z);
  and nY_nZ (nY_nZ_out, not_2_out, not_3_out);
  and X_nZ (X_nZ_out, not_3_out, X);
  and nXZ (nXZ_out, not_1_out, Z);
  or or_1 (A, XZ_out, Y);
  or or_2 (B, nX_nY_out, XYZ_out, nY_nZ_out);
  or or_3 (C, X_nZ_out, nXZ_out);

  // Notes on the sheet:
  //   XZ+Y
  //   ~X~Y+XYZ+~Y~Z
  //   X~Z+~XZ
endmodule
