// Logisim project Q1 Full Adder.circ as structural Verilog: 1 circuit, main circuit main
module main (
  input  X,
  input  Y,
  input  Z,
  output S,
  output C
);

  wire XY_out, YZ_out, Z_xor_Y_out, ZX_out;

  xor Z_xor_Y (Z_xor_Y_out, Y, Z);
  and XY (XY_out, X, Y);
  and ZX (ZX_out, X, Z);
  and YZ (YZ_out, Y, Z);
  xor xor_1 (S, X, Z_xor_Y_out);
  or or_1 (C, XY_out, ZX_out, YZ_out);
endmodule
