// Logisim project Q2 Sequential DFF.circ as structural Verilog: 1 circuit, main circuit main
module main (
  input  X,
  input  Y,
  output S,
  output Carry_Out,
  output Q
);

  wire clock_1_out, or_1_out, XY_out, YZ_out, Z_xor_Y_out, ZX_out;

  xor Z_xor_Y (Z_xor_Y_out, Y, Q);
  and XY (XY_out, X, Y);
  and ZX (ZX_out, X, Q);
  and YZ (YZ_out, Y, Q);
  Clock clock_1 (.out(clock_1_out));
  xor xor_1 (S, X, Z_xor_Y_out);
  not not_1 (Carry_Out, or_1_out);
  or or_1 (or_1_out, XY_out, ZX_out, YZ_out);
  D_Flip_Flop d_ff_1 (.clk(clock_1_out), .D(Carry_Out), .Q(Q));  // open: Qn, preset, en, reset
endmodule
