// Logisim project Q3 - Sequential.circ as structural Verilog: 1 circuit, main circuit main
module main (
  input  X,
  input  Y,
  output Z,
  output A,
  output B
);

  wire clock_1_out, not_1_out, not_2_out, nxy_2_out, nxy_out, nyA_out, nyB_out, or_2_out, or_3_out, or_4_out,
       xB_out, xy_out, yB_out;

  not not_1 (not_1_out, X);
  not not_2 (not_2_out, Y);
  and nxy (nxy_out, Y, not_1_out);
  and nxy_2 (nxy_2_out, not_1_out, Y);
  and yB (yB_out, Y, B);
  and nyB (nyB_out, not_2_out, B);
  and xy (xy_out, Y, X);
  and xB (xB_out, X, B);
  and nyA (nyA_out, not_2_out, A);
  or or_1 (Z, X, nxy_out);
  Clock clock_1 (.out(clock_1_out));
  or or_2 (or_2_out, nxy_2_out, yB_out);
  or or_3 (or_3_out, nyB_out, xy_out);
  or or_4 (or_4_out, xB_out, nyA_out);
  J_K_Flip_Flop j_k_ff_1 (.J(or_3_out), .clk(clock_1_out), .K(or_4_out), .Q(B));  // open: Qn, preset, en, reset
  D_Flip_Flop d_ff_1 (.clk(clock_1_out), .D(or_2_out), .Q(A));  // open: Qn, preset, en, reset

  // Notes on the sheet:
  //   Da = ~xy + yB
  //   JB = ~yB + xy
  //   KB = xB + ~yA
  //   z = x+~xy
endmodule
